# Fritzing sketch diagram (saved by Fritzing 0.9.9b)
breadboards: 1

parts:
  Part1 = Arduino Uno (Rev3)
  DS1 = DS18B20 1-Wire Temperature Sensor [part_number=DS18B20]
  R1 = Resistor [tolerance=±5% power=0.25 resistance=4700 package=THT]

nets:
  N1: Part1.D10_PWM/SS, DS1.VDD, R1.Pin_0
  N2: Part1.5V, DS1.DQ, R1.Pin_1
  GND: Part1.GND, DS1.GND
